# Fritzing sketch ad-connector (saved by Fritzing 0.9.1b)
circuit board: 3.0808cm x 3.2878cm
breadboards: 1

parts:
  R0 = Resistor [tolerance=±5% resistance=220 package=THT]
  BUS_CONNECTOR = AVR ISP 6 Pin [package=2x3]
  AD_Board = FTDI_BASIC [package=ftdi_basic]
  JP3 = FTDI_BASIC [package=ftdi_basic]
  BUS_CONNECTOR1 = AVR ISP 6 Pin [package=2x3]
  BUS_CONNECTOR2 = AVR ISP 6 Pin [package=2x3]
  R1 = Resistor [tolerance=±5% resistance=220 package=THT]
  R2 = Resistor [tolerance=±5% resistance=220 package=THT]
  R3 = Resistor [tolerance=±5% resistance=220 package=THT]
  JP4 = FTDI_BASIC [package=ftdi_basic]

nets:
  N1: R0.Pin_0, BUS_CONNECTOR.5, BUS_CONNECTOR.6, AD_Board.2, R1.Pin_0, R2.Pin_0, R3.Pin_0, JP4.1
  N2: R0.Pin_1, JP3.3, BUS_CONNECTOR1.1
  N3: BUS_CONNECTOR.2, AD_Board.1, BUS_CONNECTOR1.2, BUS_CONNECTOR2.2, JP4.5
  N4: BUS_CONNECTOR.3, AD_Board.4, JP4.4
  N5: BUS_CONNECTOR.4, AD_Board.3, JP4.3
  N6: JP3.5, BUS_CONNECTOR2.3, R2.Pin_1
  N7: JP3.6, BUS_CONNECTOR2.5, R3.Pin_1
  N8: JP3.4, BUS_CONNECTOR2.1, R1.Pin_1
  N9: BUS_CONNECTOR1.4, BUS_CONNECTOR2.4
  N10: BUS_CONNECTOR1.6, BUS_CONNECTOR2.6

notes:
  GND OE SCK SDA VCC V++
