# Fritzing sketch darlington-v2_upwards (saved by Fritzing 0.9.1b)
circuit board: 2.80492cm x 4.17963cm

parts:
  Darlington = Darlington Driver [package=so18l]
  Q1 = Basic FET P-Channel [package="TO220 [THT]"]
  Q2 = Basic FET P-Channel [package="TO220 [THT]"]
  Q3 = Basic FET P-Channel [package="TO220 [THT]"]
  Q4 = Basic FET P-Channel [package="TO220 [THT]"]
  Q5 = Basic FET P-Channel [package="TO220 [THT]"]
  Q6 = Basic FET P-Channel [package="TO220 [THT]"]
  Q7 = Basic FET P-Channel [package="TO220 [THT]"]
  Q8 = Basic FET P-Channel [package="TO220 [THT]"]
  Q9 = Basic FET P-Channel [package="TO220 [THT]"]
  Q10 = Basic FET P-Channel [package="TO220 [THT]"]
  Q11 = Basic FET P-Channel [package="TO220 [THT]"]
  Q12 = Basic FET P-Channel [package="TO220 [THT]"]

nets:
  N1: Darlington.1, Q5.gate
  N2: Darlington.2, Q5.drain
  N3: Darlington.3, Q5.source
  N4: Darlington.4, Q4.gate
  N5: Darlington.5, Q3.gate
  N6: Darlington.6, Q3.drain
  N7: Darlington.7, Q3.source
  N8: Darlington.8, Q2.gate
  N9: Darlington.9, Q1.source
  N10: Darlington.10, Q9.gate, Q9.drain, Q10.gate, Q10.drain, Q10.source, Q11.gate, Q11.drain, Q11.source, Q12.drain
  N11: Darlington.11, Q7.gate
  N12: Darlington.12, Q7.drain
  N13: Darlington.13, Q8.source
  N14: Darlington.14, Q8.drain
  N15: Darlington.15, Q8.gate
  N16: Darlington.16, Q6.source
  N17: Darlington.17, Q6.drain
  N18: Darlington.18, Q6.gate
