# Fritzing sketch darlington (saved by Fritzing 0.9.0b)
circuit board: 10.1776cm x 5.36194cm
breadboards: 1

parts:
  U13 = AVR 10-pin ICSP Header [package="avr icsp"]  # not connected
  U14 = AVR 10-pin ICSP Header [package="avr icsp"]  # not connected
  U15 = AVR 10-pin ICSP Header [package="avr icsp"]  # not connected
  U16 = AVR 10-pin ICSP Header [package="avr icsp"]  # not connected
  ULN6 = Darlington Driver [package=so018]
  ULN8 = Darlington Driver [package=so018]
  ULN7 = Darlington Driver [package=so018]
  ULN5 = Darlington Driver [package=so018]
  IC1 = SHIFT REGISTER [package=so16]
  IC2 = SHIFT REGISTER [package=so16]
  IC3 = SHIFT REGISTER [package=so16]
  IC4 = SHIFT REGISTER [package=so16]
  Part3 = YC164 [package=YC164]  # not connected
  LED_CLK = LEDs [package=led-1206]  # not connected
  LED_SIN = LEDs [package=led-1206]  # not connected
  LED_LE = LEDs [package=led-1206]  # not connected
  LED_OE = LEDs [package=led-1206]  # not connected
  Part2 = Arduino Mega 2560 (Rev3)
  USB1_IN = USB_MICROB_PLUG [package=micro-b-th]  # not connected
  USB2_IN = USB_MICROB_PLUG [package=micro-b-th]  # not connected

nets:
  N1: ULN6.1, IC3.QH
  N2: ULN6.2, IC3.QG
  N3: ULN6.3, IC3.QF
  N4: ULN6.4, IC3.QE
  N5: ULN6.5, IC3.QD
  N6: ULN6.6, IC3.QC
  N7: ULN6.7, IC3.QB
  N8: ULN6.8, IC3.QA
  N9: ULN8.1, IC4.QH
  N10: ULN8.2, IC4.QG
  N11: ULN8.3, IC4.QF
  N12: ULN8.4, IC4.QE
  N13: ULN8.5, IC4.QD
  N14: ULN8.6, IC4.QC
  N15: ULN8.7, IC4.QB
  N16: ULN8.8, IC4.QA
  GND: ULN8.9, ULN7.9, IC2.GND, IC2.SCL, IC4.GND, IC4.SCL, Part2.GND
  N17: ULN7.1, IC2.QH
  N18: ULN7.2, IC2.QG
  N19: ULN7.3, IC2.QF
  N20: ULN7.4, IC2.QE
  N21: ULN7.5, IC2.QD
  N22: ULN7.6, IC2.QC
  N23: ULN7.7, IC2.QB
  N24: ULN7.8, IC2.QA
  N25: ULN5.1, IC1.QH
  N26: ULN5.2, IC1.QG
  N27: ULN5.3, IC1.QF
  N28: ULN5.4, IC1.QE
  N29: ULN5.5, IC1.QD
  N30: ULN5.6, IC1.QC
  N31: ULN5.7, IC1.QB
  N32: ULN5.8, IC1.QA
  N33: IC2.SCK, Part2.D35
  N34: IC2.RCK, Part2.D36
  N35: IC2.G, Part2.D11_PWM
  N36: IC2.SER, Part2.D34
  VCC: IC2.VCC, IC4.VCC, Part2.5V
  N37: IC4.SCK, Part2.D31
  N38: IC4.RCK, Part2.D32
  N39: IC4.G, Part2.D10_PWM
  N40: IC4.SER, Part2.D30
