# Fritzing sketch darlington (saved by Fritzing 0.9.0b)
circuit board: 10.1776cm x 5.36194cm
breadboards: 1

parts:
  U13 = AVR 10-pin ICSP Header [package="avr icsp"]
  U14 = AVR 10-pin ICSP Header [package="avr icsp"]
  ULN6 = Darlington Driver [package=so018]
  ULN8 = Darlington Driver [package=so018]
  ULN7 = Darlington Driver [package=so018]
  ULN5 = Darlington Driver [package=so018]
  USB1_IN = USB_MICROB_PLUG [package=micro-b-th]
  USB2_IN = USB_MICROB_PLUG [package=micro-b-th]
  Part2 = Arduino Mega 2560 (Rev3)
  IC4 = SHIFT REGISTER [package=so16]
  JP2 = Header 2 [package=molex-1x2_lock]
  JP3 = Header 2 [package=molex-1x2_lock]
  IC2 = SHIFT REGISTER [package=so16]
  C1 = Ceramic Capacitor [capacitance="100 nF" package="0603 [SMD, multilayer]"]
  U16 = AVR 10-pin ICSP Header [package="avr icsp"]
  U15 = AVR 10-pin ICSP Header [package="avr icsp"]
  LED1 = smd LED [color="Red (633nm)" package="1206 [SMD]"]
  R3 = Resistor [tolerance=±5% resistance=220 package="0805 [SMD]"]
  R6 = Resistor [tolerance=±5% resistance=220 package="0805 [SMD]"]
  LED3 = smd LED [color="Red (633nm)" package="1206 [SMD]"]
  J1 = AVR ISP 6 Pin [package=2x3]  # not connected
  J2 = AVR ISP 6 Pin [package=2x3]  # not connected

nets:
  N1: U13.1, U13.2, ULN6.10, JP3.2, C1.1
  N2: U13.3, ULN6.11
  N3: U13.4, ULN6.12
  N4: U13.5, ULN6.13
  N5: U13.6, ULN6.14
  N6: U13.7, ULN6.15
  N7: U13.8, ULN6.16
  N8: U13.9, ULN6.17
  N9: U13.10, ULN6.18
  N10: U14.1, U14.2, ULN5.10, JP2.2
  N11: U14.3, ULN5.11
  N12: U14.4, ULN5.12
  N13: U14.5, ULN5.13
  N14: U14.6, ULN5.14
  N15: U14.7, ULN5.15
  N16: U14.8, ULN5.16
  N17: U14.9, ULN5.17
  N18: U14.10, ULN5.18
  N19: ULN6.1, Part2.D37
  N20: ULN6.2, Part2.D36
  N21: ULN6.3, Part2.D35
  N22: ULN6.4, Part2.D34
  N23: ULN6.5, Part2.D33
  N24: ULN6.6, Part2.D32
  N25: ULN6.7, Part2.D31
  N26: ULN6.8, Part2.D30
  N27: ULN6.9, JP3.1, C1.0
  N28: ULN8.1, IC4.QH
  N29: ULN8.2, IC4.QG
  N30: ULN8.3, IC4.QF
  N31: ULN8.4, IC4.QE
  N32: ULN8.5, IC4.QD
  N33: ULN8.6, IC4.QC
  N34: ULN8.7, IC4.QB
  N35: ULN8.8, IC4.QA
  GND: ULN8.9, ULN7.9, USB1_IN.GND, USB2_IN.GND, Part2.GND, IC4.GND, IC4.SCL, IC2.GND, IC2.SCL, R3.Pin_1, R6.Pin_1
  VCC: ULN8.10, USB2_IN.VCC, IC4.VCC, U16.1, U16.2
  N36: ULN8.11, U16.3
  N37: ULN8.12, U16.4
  N38: ULN8.13, U16.5
  N39: ULN8.14, U16.6
  N40: ULN8.15, U16.7
  N41: ULN8.16, U16.8
  N42: ULN8.17, U16.9
  N43: ULN8.18, U16.10
  N44: ULN7.1, IC2.QH
  N45: ULN7.2, IC2.QG
  N46: ULN7.3, IC2.QF
  N47: ULN7.4, IC2.QE
  N48: ULN7.5, IC2.QD
  N49: ULN7.6, IC2.QC
  N50: ULN7.7, IC2.QB
  N51: ULN7.8, IC2.QA
  VCC_2: ULN7.10, USB1_IN.VCC, IC2.VCC, U15.1, U15.2, LED3.cathode
  N52: ULN7.11, U15.3
  N53: ULN7.12, U15.4
  N54: ULN7.13, U15.5
  N55: ULN7.14, U15.6
  N56: ULN7.15, U15.7
  N57: ULN7.16, U15.8
  N58: ULN7.17, U15.9
  N59: ULN7.18, U15.10
  N60: ULN5.1, Part2.D45
  N61: ULN5.2, Part2.D44
  N62: ULN5.3, Part2.D43
  N63: ULN5.4, Part2.D42
  N64: ULN5.5, Part2.D41
  N65: ULN5.6, Part2.D40
  N66: ULN5.7, Part2.D39
  N67: ULN5.8, Part2.D38
  N68: ULN5.9, JP2.1
  N69: Part2.D11_PWM, IC2.G
  N70: Part2.D10_PWM, IC4.G
  N71: Part2.D46, IC2.SER
  N72: Part2.D47, IC2.RCK
  N73: Part2.D48, IC2.SCK
  N74: Part2.D50, IC4.SER
  N75: Part2.D51, IC4.RCK
  N76: Part2.D52, IC4.SCK
  N77: LED1.anode, R3.Pin_0
  N78: R6.Pin_0, LED3.anode

notes:
  2014-11-25
  sixthsense
  +/-
  0
