# Fritzing sketch h-bridge (saved by Fritzing 0.9.0b)
breadboards: 2

parts:
  U1 = L298_BRIDGE_DRIVER [package=powerso20]
  U2 = L298_BRIDGE_DRIVER [package=powerso20]
  U3 = L298_BRIDGE_DRIVER [package=powerso20]
  U4 = L298_BRIDGE_DRIVER [package=powerso20]
  Peltier_LEFT = AVR 10-pin ICSP Header [package="avr icsp"]  # not connected
  Peltier_RIGHT = AVR 10-pin ICSP Header [package="avr icsp"]
  Part1 = Arduino Mega 2560 (Rev3)
  U6 = 74HC04_HEX_INVERTER [package=dil14]
  U7 = 74HC04_HEX_INVERTER [package=dil14]
  X1 = USB Connectors [package=usb-microb]  # not connected
  X2 = USB Connectors [package=usb-microb]  # not connected
  X3 = USB Connectors [package=usb-microb]  # not connected

nets:
  GND: U1.GND, U1.SENSE_A, U1.SENSE_B, U2.GND, U2.SENSE_A, U2.SENSE_B, U3.GND, U3.SENSE_A, U3.SENSE_B, U4.GND, U4.SENSE_A, U4.SENSE_B, Part1.GND, U6.GND, U7.GND
  N1: U1.OUT1, Peltier_RIGHT.5
  N2: U1.OUT2, Peltier_RIGHT.6
  N3: U1.IN1, Part1.D24, U6.2A
  N4: U1.ENA, Part1.D4_PWM
  N5: U1.IN2, U6.2Y
  VSS: U1.VSS, U2.VSS, U3.VSS, U4.VSS, Part1.5V, U6.VCC, U7.VCC
  N6: U1.IN3, Part1.D25, U6.5A
  N7: U1.ENB, Part1.D5_PWM
  N8: U1.IN4, U6.5Y
  N9: U2.OUT1, Peltier_RIGHT.3
  N10: U2.OUT2, Peltier_RIGHT.4
  N11: U2.IN1, Part1.D22, U6.1A
  N12: U2.ENA, Part1.D2_PWM
  N13: U2.IN2, U6.1Y
  N14: U2.IN3, Part1.D23, U6.6A
  N15: U2.ENB, Part1.D3_PWM
  N16: U2.IN4, U6.6Y
  N17: U3.OUT1, Peltier_RIGHT.9
  N18: U3.OUT2, Peltier_RIGHT.10
  N19: U3.IN1, Part1.D28, U7.2A
  N20: U3.ENA, Part1.D12_PWM
  N21: U3.IN2, U7.2Y
  N22: U3.IN3, Part1.D29, U7.5A
  N23: U3.ENB, Part1.D13_PWM
  N24: U3.IN4, U7.6Y
  N25: U4.OUT1, Peltier_RIGHT.7
  N26: U4.OUT2, Peltier_RIGHT.8
  N27: U4.IN1, Part1.D26, U7.1A
  N28: U4.ENA, Part1.D6_PWM
  N29: U4.IN2, U7.1Y
  N30: U4.IN3, Part1.D27, U7.6A
  N31: U4.ENB, Part1.D7_PWM
  N32: U4.IN4, U7.5Y
