# Fritzing sketch connector_right (saved by Fritzing 0.9.0b)
circuit board: 2.03731cm x 3.01739cm

parts:
  U1 = Voltage Regulator - 5V [package="TO220 [THT]"]
  PWM_Board = Voltage Regulator - 5V [package="TO220 [THT]"]
  Connector = AVR ISP 6 Pin [package=2x3-ns]
  POWER = LED - 5mm [color="Red (633nm)" package="5 mm [THT]"]

nets:
  N1: U1.input_voltage, Connector.5, Connector.6, POWER.cathode
  N2: U1.output_voltage, Connector.3
  N3: PWM_Board.input_voltage, Connector.1, POWER.anode
  N4: PWM_Board.GND, Connector.2
  N5: PWM_Board.output_voltage, Connector.4

notes:
  V++ GND
