# Fritzing sketch darlington-winkel (saved by Fritzing 0.9.0b)
circuit board: 10.1776cm x 5.36194cm
breadboards: 1

parts:
  U13 = AVR 10-pin ICSP Header [package="avr icsp"]
  U14 = AVR 10-pin ICSP Header [package="avr icsp"]
  Part2 = Arduino Mega 2560 (Rev3)
  IC4 = SHIFT REGISTER [package=so16]
  JP2 = Header 2 [package=molex-1x2_lock]
  JP3 = Header 2 [package=molex-1x2_lock]
  U16 = AVR 10-pin ICSP Header [package="avr icsp"]
  U15 = AVR 10-pin ICSP Header [package="avr icsp"]
  LED1 = smd LED [color="Red (633nm)" package="1206 [SMD]"]
  R3 = Resistor [tolerance=±5% resistance=220 package="0805 [SMD]"]
  R6 = Resistor [tolerance=±5% resistance=220 package="0805 [SMD]"]
  LED3 = smd LED [color="Red (633nm)" package="1206 [SMD]"]
  J1 = AVR ISP 6 Pin [package=2x3]  # not connected
  J2 = AVR ISP 6 Pin [package=2x3]  # not connected
  ULN7 = Darlington Driver [package=so18l]
  IC2 = SHIFT REGISTER [package=so16]
  ULN8 = Darlington Driver [package=so18l]
  ULN6 = Darlington Driver [package=so18l]
  ULN5 = Darlington Driver [package=so18l]
  U17 = USB Connectors [package=usb-microb]
  U18 = USB Connectors [package=usb-microb]
  C1 = Ceramic Capacitor [capacitance="100 nF" package="1206 [SMD, multilayer]"]
  C2 = Ceramic Capacitor [capacitance="100 nF" package="1206 [SMD, multilayer]"]

nets:
  N1: U13.1, U13.2, JP3.2, ULN6.10, C1.1
  N2: U13.3, ULN6.11
  N3: U13.4, ULN6.12
  N4: U13.5, ULN6.13
  N5: U13.6, ULN6.14
  N6: U13.7, ULN6.15
  N7: U13.8, ULN6.16
  N8: U13.9, ULN6.17
  N9: U13.10, ULN6.18
  N10: U14.1, U14.2, JP2.2, ULN5.10, C2.1
  N11: U14.3, ULN5.11
  N12: U14.4, ULN5.12
  N13: U14.5, ULN5.13
  N14: U14.6, ULN5.14
  N15: U14.7, ULN5.15
  N16: U14.8, ULN5.16
  N17: U14.9, ULN5.17
  N18: U14.10, ULN5.18
  N19: Part2.D11_PWM, IC2.G
  N20: Part2.D10_PWM, IC4.G
  GND: Part2.GND, IC4.GND, R3.Pin_1, R6.Pin_1, ULN7.9, IC2.GND, ULN8.9, U17.GND, U18.GND
  N21: Part2.D30, ULN6.8
  N22: Part2.D31, ULN6.7
  N23: Part2.D32, ULN6.6
  N24: Part2.D33, ULN6.5
  N25: Part2.D34, ULN6.4
  N26: Part2.D35, ULN6.3
  N27: Part2.D36, ULN6.2
  N28: Part2.D37, ULN6.1
  N29: Part2.D38, ULN5.8
  N30: Part2.D39, ULN5.7
  N31: Part2.D40, ULN5.6
  N32: Part2.D41, ULN5.5
  N33: Part2.D42, ULN5.4
  N34: Part2.D43, ULN5.3
  N35: Part2.D44, ULN5.2
  N36: Part2.D45, ULN5.1
  N37: Part2.D46, IC2.SER
  N38: Part2.D47, IC2.RCK
  N39: Part2.D48, IC2.SCK
  N40: Part2.D50, IC4.SER
  N41: Part2.D51, IC4.RCK
  N42: Part2.D52, IC4.SCK
  N43: IC4.QB, ULN8.7
  N44: IC4.QC, ULN8.6
  N45: IC4.QD, ULN8.5
  N46: IC4.QE, ULN8.4
  N47: IC4.QF, ULN8.3
  N48: IC4.QG, ULN8.2
  N49: IC4.QH, ULN8.1
  N50: IC4.SCL, IC4.VCC, U16.1, U16.2, LED1.cathode, ULN8.10, U18.VBUS
  N51: IC4.QA, ULN8.8
  N52: JP2.1, ULN5.9, C2.0
  N53: JP3.1, ULN6.9, C1.0
  N54: U16.3, ULN8.18
  N55: U16.4, ULN8.17
  N56: U16.5, ULN8.16
  N57: U16.6, ULN8.15
  N58: U16.7, ULN8.14
  N59: U16.8, ULN8.13
  N60: U16.9, ULN8.12
  N61: U16.10, ULN8.11
  N62: U15.1, U15.2, LED3.cathode, ULN7.10, IC2.SCL, IC2.VCC, U17.VBUS
  N63: U15.3, ULN7.18
  N64: U15.4, ULN7.17
  N65: U15.5, ULN7.16
  N66: U15.6, ULN7.15
  N67: U15.7, ULN7.14
  N68: U15.8, ULN7.13
  N69: U15.9, ULN7.12
  N70: U15.10, ULN7.11
  N71: LED1.anode, R3.Pin_0
  N72: R6.Pin_0, LED3.anode
  N73: ULN7.1, IC2.QH
  N74: ULN7.2, IC2.QG
  N75: ULN7.3, IC2.QF
  N76: ULN7.4, IC2.QE
  N77: ULN7.5, IC2.QD
  N78: ULN7.6, IC2.QC
  N79: ULN7.7, IC2.QB
  N80: ULN7.8, IC2.QA

notes:
  2014-11-25
  sixthsense
  -
  0
  +
