# Fritzing sketch i2c_shield (saved by Fritzing 0.9.1b)
circuit board: 10.1776cm x 5.36194cm
breadboards: 1

parts:
  Part1 = Arduino Mega 2560 (Rev3)
  J1 = AVR ISP 6 Pin [package=2x3-ns]
  J2 = AVR ISP 6 Pin [package=2x3-ns]
  J3 = AVR ISP 6 Pin [package=2x3-ns]
  J4 = AVR ISP 6 Pin [package=2x3-ns]
  U19 = USB Connectors [package=usb-microb]
  U20 = USB Connectors [package=usb-microb]
  U21 = USB Connectors [package=usb-microb]
  U22 = USB Connectors [package=usb-microb]
  PCB1 = Arduino Mega Shield PCB  # not connected
  J5 = AVR ISP 6 Pin [package=2x3-ns]
  U24 = Voltage Regulator - 5V [package="TO220 [THT]"]
  U23 = Voltage Regulator - 5V [package="TO220 [THT]"]
  J6 = AVR ISP 6 Pin [package=2x3-ns]
  VCC1 = Battery
  VCC2 = Battery
  J7 = AVR ISP 6 Pin [package=2x3-ns]

nets (from the pcb view):
  N1: Part1.D21/SCL, Part1.SCL, J1.4, J2.4, J3.4, J4.4, J5.4, J6.4
  N2: Part1.D20/SDA, Part1.SDA, J1.3, J2.3, J3.3, J4.3, J5.3, J6.3
  N3: Part1.D19/RX1, J7.5, J7.6
  N4: Part1.D18/TX1, J7.1, J7.2
  GND: Part1.GND, J1.5, J1.6, J2.5, J2.6, J3.5, J3.6, J4.5, J4.6, U19.GND, U20.GND, U21.GND, U22.GND, J5.5, J5.6, U24.GND, J6.5, J6.6, VCC1.-, VCC2.-
  N5: Part1.IOREF, J1.2, J2.2, J3.2, J4.2
  N6: Part1.5V, J5.2, U24.input_voltage, J6.2
  N7: J1.1, U19.VBUS
  N8: J2.1, U20.VBUS
  N9: J3.1, U21.VBUS
  N10: J4.1, U22.VBUS
  N11: J5.1, VCC1.+
  N12: U24.output_voltage, J7.3
  N13: U23.output_voltage, J7.4
  N14: J6.1, VCC2.+

notes:
  RT PQ RX TX GND VCC
  sixthsense

custom parts:
  Arduino Mega Shield PCB: Plain PCB Shaped to fit an Arduino Mega R3 "Shield"
