# Fritzing sketch connector_left_top_mount (saved by Fritzing 0.9.1b)
circuit board: 2.05833cm x 3.25181cm

parts:
  U1 = Voltage Regulator - 5V [package="TO220 [THT]"]
  PWM_Board = Voltage Regulator - 5V [package="TO220 [THT]"]
  Connector = AVR ISP 6 Pin [package=2x3-ns]
  POWER = LED - 5mm [color="Red (633nm)" package="5 mm [THT]"]
  Q1 = Basic FET P-Channel [package="TO220 [THT]"]

nets:
  N1: U1.input_voltage, Connector.5, Connector.6, POWER.anode
  N2: U1.output_voltage, Connector.4
  N3: PWM_Board.input_voltage, Q1.drain
  N4: PWM_Board.GND, Connector.2
  N5: PWM_Board.output_voltage, Connector.3
  N6: Connector.1, Q1.gate
  N7: POWER.cathode, Q1.source

notes:
  V++ GND
  GND OE SCK SDA VCC V++
