# Fritzing sketch connector_right_bottom_mount (saved by Fritzing 0.9.1b)
circuit board: 2.15013cm x 3.80325cm

parts:
  U1 = Voltage Regulator - 5V [package="TO220 [THT]"]
  PWM_Board = Voltage Regulator - 5V [package="TO220 [THT]"]
  Connector = AVR ISP 6 Pin [package=2x3-ns]
  POWER = LED - 5mm [color="Red (633nm)" package="5 mm [THT]"]
  PWM_Board1 = Voltage Regulator - 5V [package="TO220 [THT]"]
  U2 = Voltage Regulator - 5V [package="TO220 [THT]"]
  U3 = Voltage Regulator - 5V [package="TO220 [THT]"]

nets:
  N1: U1.input_voltage, Connector.1, Connector.2, POWER.cathode, U2.input_voltage
  N2: U1.output_voltage, Connector.4, U2.output_voltage
  N3: PWM_Board.input_voltage, PWM_Board1.input_voltage, U3.GND
  GND: PWM_Board.GND, Connector.6, PWM_Board1.GND
  N4: PWM_Board.output_voltage, Connector.3, PWM_Board1.output_voltage
  N5: Connector.5, U3.input_voltage
  N6: POWER.anode, U3.output_voltage

notes:
  V++ GND
  GND OE SCK SDA VCC V++
